# Fritzing sketch 5Leds (saved by Fritzing 0.9.2b)
breadboards: 1

parts:
  ARDUINO_UNO = Arduino Uno (Rev3)
  R1 = Resistor [tolerance=±5% resistance=220 package=THT]
  R2 = Resistor [tolerance=±5% resistance=220 package=THT]
  R3 = Resistor [tolerance=±5% resistance=220 package=THT]
  R4 = Resistor [tolerance=±5% resistance=220 package=THT]
  R5 = Resistor [tolerance=±5% resistance=220 package=THT]
  LED1 = LED - 5mm [color="Red (633nm)" package="5 mm [THT]"]
  LED2 = LED - 5mm [color="Red (633nm)" package="5 mm [THT]"]
  LED3 = LED - 5mm [color="Red (633nm)" package="5 mm [THT]"]
  LED4 = LED - 5mm [color="Red (633nm)" package="5 mm [THT]"]
  LED5 = LED - 5mm [color="Red (633nm)" package="5 mm [THT]"]

nets:
  N1: ARDUINO_UNO.D2, R1.Pin_1
  N2: ARDUINO_UNO.D3_PWM, R2.Pin_1
  N3: ARDUINO_UNO.D4, R3.Pin_1
  N4: ARDUINO_UNO.D5_PWM, R4.Pin_1
  N5: ARDUINO_UNO.D6_PWM, R5.Pin_1
  N6: ARDUINO_UNO.GND, LED1.anode, LED2.anode, LED3.anode, LED4.anode, LED5.anode
  N7: R1.Pin_0, LED1.cathode
  N8: R2.Pin_0, LED2.cathode
  N9: R3.Pin_0, LED3.cathode
  N10: R4.Pin_0, LED4.cathode
  N11: R5.Pin_0, LED5.cathode
